# Fritzing sketch dice (saved by Fritzing 0.9.3b)
breadboards: 1

parts:
  Часть1 = Arduino Nano (Rev3.0)
  U3 = 74HC595 SMD [package="SO16 [SMD]"]
  LED1 = smd LED [color="Red (633nm)" package="0603 [SMD]"]
  LED2 = smd LED [color="Red (633nm)" package="0603 [SMD]"]
  LED3 = smd LED [color="Red (633nm)" package="0603 [SMD]"]
  LED4 = smd LED [color="Red (633nm)" package="0603 [SMD]"]
  LED5 = smd LED [color="Red (633nm)" package="0603 [SMD]"]
  LED6 = smd LED [color="Red (633nm)" package="0603 [SMD]"]
  LED7 = smd LED [color="Red (633nm)" package="0603 [SMD]"]
  R1 = Resistor [tolerance=±5% resistance=220 package="2010 [SMD]"]
  R2 = Resistor [tolerance=±5% resistance=220 package="2010 [SMD]"]
  R3 = Resistor [tolerance=±5% resistance=220 package="2010 [SMD]"]
  R4 = Resistor [tolerance=±5% resistance=220 package="2010 [SMD]"]
  R5 = Resistor [tolerance=±5% resistance=220 package="2010 [SMD]"]
  R6 = Resistor [tolerance=±5% resistance=220 package="2010 [SMD]"]
  R7 = Resistor [tolerance=±5% resistance=220 package="2010 [SMD]"]
  S1 = Pushbutton [package="[SMD]"]
  R8 = Resistor [tolerance=±5% resistance=1k package="2010 [SMD]"]
  S2 = Pushbutton [package="[SMD]"]
  R9 = Resistor [tolerance=±5% resistance=1k package="2010 [SMD]"]
  S3 = Pushbutton [package="[SMD]"]
  R10 = Resistor [tolerance=±5% resistance=1k package="2010 [SMD]"]

nets:
  GND: Часть1.GND, U3.GND, U3.OE, LED1.cathode, LED2.cathode, LED3.cathode, LED4.cathode, LED5.cathode, LED6.cathode, LED7.cathode, R9.Pin_1, R10.Pin_1
  N1: Часть1.D2, S3.Pin_1, S3.Pin_2, R10.Pin_0
  N2: Часть1.D3, S2.Pin_1, S2.Pin_2, R9.Pin_0
  N3: Часть1.D4, S1.Pin_1, S1.Pin_2, R8.Pin_0
  N4: Часть1.D8, U3.DS
  N5: Часть1.D9, U3.ST_CP
  N6: Часть1.D10, U3.SH_CP
  5V: Часть1.5V, U3.MR, U3.VCC, S1.Pin_3, S1.Pin_4, S2.Pin_3, S2.Pin_4, S3.Pin_3, S3.Pin_4
  N7: U3.Q1, R7.Pin_1
  N8: U3.Q2, R6.Pin_1
  N9: U3.Q3, R5.Pin_1
  N10: U3.Q4, R1.Pin_1
  N11: U3.Q5, R2.Pin_1
  N12: U3.Q6, R3.Pin_1
  N13: U3.Q7, R4.Pin_1
  N14: LED1.anode, R7.Pin_0
  N15: LED2.anode, R1.Pin_0
  N16: LED3.anode, R2.Pin_0
  N17: LED4.anode, R5.Pin_0
  N18: LED5.anode, R6.Pin_0
  N19: LED6.anode, R3.Pin_0
  N20: LED7.anode, R4.Pin_0
